// Logisim project ALU.circ as structural Verilog: 1 circuit, main circuit main
module main (
  input  Cin,
  input  [3:0] A,
  input  [3:0] B,
  input  [1:0] s2,
  input  [1:0] s1,
  input  [1:0] in_6,
  input  _0___Left,
  output [3:0] F,
  output Cout
);

  wire adder_1_cout, adder_2_cout, adder_3_cout, multiplexer_1_out, multiplexer_2_out, multiplexer_3_out,
       multiplexer_4_out, multiplexer_5_out, multiplexer_6_out, not_1_out, not_2_out, not_3_out, not_4_out,
       not_5_out, not_6_out;
  wire [3:0] adder_1_out, and_1_out, multiplexer_7_out, multiplexer_11_out, not_7_out, or_1_out, xor_1_out;

  not not_1 (not_1_out, B[0]);
  not not_2 (not_2_out, B[1]);
  not not_3 (not_3_out, B[2]);
  not not_4 (not_4_out, B[3]);
  not not_5 (not_5_out, 1'b1);
  not not_6 (not_6_out, 1'b1);
  Multiplexer #(.select(2)) multiplexer_1 (
    .in0(not_5_out), .in1(A[3]), .in2(A[0]), .out(multiplexer_1_out), .sel(in_6));  // open: in3, en
  Multiplexer #(.select(2)) multiplexer_2 (
    .in0(not_5_out), .in1(A[0]), .in2(not_5_out), .out(multiplexer_2_out), .sel(in_6));  // open: in3, en
  assign and_1_out = A & B;  // AND_Gate and_1, 4 bits wide
  assign or_1_out = A | B;  // OR_Gate or_1, 4 bits wide
  assign xor_1_out = A ^ B;  // XOR_Gate xor_1, 4 bits wide
  assign not_7_out = ~A;  // NOT_Gate not_7, 4 bits wide
  Multiplexer #(.select(2)) multiplexer_3 (
    .in0(B[0]), .in1(not_1_out), .in2(not_6_out), .in3(1'b1), .out(multiplexer_3_out), .sel(s1));  // open: en
  Multiplexer #(.select(2)) multiplexer_4 (
    .in0(B[1]), .in1(not_2_out), .in2(not_6_out), .in3(1'b1), .out(multiplexer_4_out), .sel(s1));  // open: en
  Multiplexer #(.select(2)) multiplexer_5 (
    .in0(B[2]), .in1(not_3_out), .in2(not_6_out), .in3(1'b1), .out(multiplexer_5_out), .sel(s1));  // open: en
  Multiplexer #(.select(2)) multiplexer_6 (
    .in0(B[3]), .in1(not_4_out), .in2(not_6_out), .in3(1'b1), .out(multiplexer_6_out), .sel(s1));  // open: en
  Multiplexer multiplexer_7 (
    .in0(multiplexer_1_out), .in1(A[1]), .out(multiplexer_7_out[0]), .sel(_0___Left));  // open: en
  Multiplexer multiplexer_8 (.in0(A[0]), .in1(A[2]), .out(multiplexer_7_out[1]), .sel(_0___Left));  // open: en
  Multiplexer multiplexer_9 (.in0(A[1]), .in1(A[3]), .out(multiplexer_7_out[2]), .sel(_0___Left));  // open: en
  Multiplexer multiplexer_10 (
    .in0(A[2]), .in1(multiplexer_2_out), .out(multiplexer_7_out[3]), .sel(_0___Left));  // open: en
  Adder #(.width(1)) adder_1 (.a(A[0]), .b(multiplexer_3_out), .out(adder_1_out[0]), .cin(Cin), .cout(adder_1_cout));
  Adder #(.width(1)) adder_2 (
    .a(A[1]), .b(multiplexer_4_out), .out(adder_1_out[1]), .cin(adder_1_cout), .cout(adder_2_cout));
  Adder #(.width(1)) adder_3 (
    .a(A[2]), .b(multiplexer_5_out), .out(adder_1_out[2]), .cin(adder_2_cout), .cout(adder_3_cout));
  Adder #(.width(1)) adder_4 (.a(A[3]), .b(multiplexer_6_out), .out(adder_1_out[3]), .cin(adder_3_cout), .cout(Cout));
  Multiplexer #(.select(2), .width(4)) multiplexer_11 (
    .in0(and_1_out), .in1(or_1_out), .in2(xor_1_out), .in3(not_7_out), .out(multiplexer_11_out), .sel(s1));  // open: en
  Multiplexer #(.select(2), .width(4)) multiplexer_12 (
    .in0(adder_1_out), .in1(multiplexer_11_out), .in2(multiplexer_7_out), .out(F), .sel(s2));  // open: in3, en

  // Notes on the sheet:
  //   00 : Logical Shift
  //   01 : Circular Shift
  //   10 : Arithmetic Shift
  //   1 : Right
  //   Arithmetic Logic Shift Unit
  //   Logic
  //   Arithmetic
  //   Shift
  //   s3
  //   s0
endmodule
